# Fritzing sketch Sketch_230727 (saved by Fritzing 0.9.3b)

parts:
  부품1 = Arduino Uno (Rev3)
  부품2 = Arduino Mega 2560 (Rev3)
  M1 = DC Motor
  M2 = DC Motor
  M3 = DC Motor
  M4 = DC Motor
  S1 = H-Bridge with L298N
  S2 = H-Bridge with L298N
  부품3 = InvenSense MPU6050

nets:
  N1: 부품1.A4/SDA, 부품3.SDA
  N2: 부품1.A5/SCL, 부품3.SCL
  N3: 부품1.D2, 부품3.INT
  5V: 부품1.5V, S2.5V
  GND: 부품1.GND, S2.GND, 부품3.GND
  VIN: 부품1.VIN, 부품3.VCC
  N4: 부품2.D11_PWM, S2.ENB
  N5: 부품2.D10_PWM, S2.ENA
  N6: 부품2.D9_PWM, S1.ENA
  N7: 부품2.D8_PWM, S1.ENB
  N8: 부품2.D30, S1.IN4
  N9: 부품2.D31, S1.IN3
  N10: 부품2.D32, S1.IN1
  N11: 부품2.D33, S1.IN2
  N12: 부품2.D34, S2.IN1
  N13: 부품2.D35, S2.IN2
  N14: 부품2.D36, S2.IN3
  N15: 부품2.D37, S2.IN4
  N16: M1.pin_1, S1.M2-02
  N17: M1.pin_2, S1.M2-01
  N18: M2.pin_1, S2.M1-02
  N19: M2.pin_2, S2.M1-01
  N20: M3.pin_1, S1.M1-02
  N21: M3.pin_2, S1.M1-01
  N22: M4.pin_1, S2.M2-02
  N23: M4.pin_2, S2.M2-01

custom parts:
  H-Bridge with L298N: h-bridge
